# Fritzing sketch Ejercicio09-Lectura_potenciometro_LED (saved by Fritzing 0.9.3b)
breadboards: 1

parts:
  Parte1 = Arduino Uno (Rev3)
  R7 = Rotary Potentiometer (Small) [maximum_resistance=10kΩ package=THT]
  1_2x8_V_battery_pack = 2.1mm DC Barrel Jack  # not connected
  R5 = Resistor [tolerance=±5% resistance=10k package="0805 [SMD]"]
  LED1 = LED - 5mm [color="Green (555nm)" package="5 mm [THT]"]
  R6 = Resistor [tolerance=±5% resistance=220 package=THT]
  ON/OFF = Pushbutton [package="[THT]"]

nets:
  N1: Parte1.A1, R7.wiper
  N2: Parte1.D10_PWM/SS, R6.Pin_1
  N3: Parte1.D12/MISO, R5.Pin_0, ON/OFF.Pin_1, ON/OFF.Pin_2
  N4: Parte1.GND, R7.leg1, R7.leg2, LED1.cathode
  N5: Parte1.5V, ON/OFF.Pin_3, ON/OFF.Pin_4
  N6: LED1.anode, R6.Pin_0

custom parts:
  2.1mm DC Barrel Jack: 2.1mm DC Barrel Jack with Thru-Hole Connectors (breadboardable)
