# Fritzing sketch Ejercicio10-cuentapulsos_manual (saved by Fritzing 0.9.3b)
breadboards: 1

parts:
  Parte1 = Arduino Uno (Rev3)
  pulsos_INPUT_PULLUP = Pushbutton [package="[THT]"]
  LED1 = LED - 5mm [color="Red (633nm)" package="5 mm [THT]"]
  R6 = Resistor [tolerance=±5% resistance=220 package=THT]

nets:
  N1: Parte1.D10_PWM/SS, pulsos_INPUT_PULLUP.Pin_3, pulsos_INPUT_PULLUP.Pin_4
  N2: Parte1.D11_PWM/MOSI, R6.Pin_0
  N3: Parte1.GND, pulsos_INPUT_PULLUP.Pin_1, pulsos_INPUT_PULLUP.Pin_2, LED1.cathode
  N4: LED1.anode, R6.Pin_1
