# Fritzing sketch Ejercicio11-LM393_cuentapulsos (saved by Fritzing 0.9.3b)
breadboards: 1

parts:
  Parte1 = Arduino Uno (Rev3)
  TCRT1 = TCRT5000 (LM393) [chip_label=TCRT5000 package="DIP (Dual Inline) [THT]"]

nets:
  N1: Parte1.A5/SCL, TCRT1.A0
  N2: Parte1.D2, TCRT1.D0
  5V: Parte1.5V, TCRT1.Vcc
  GND: Parte1.GND, TCRT1.GND

custom parts:
  TCRT5000 (LM393): Sensor de infrarrojos para seguir líneas. Válido también para representar encoder de pulsos: optoacoplador FC-03 (ó FZ0888) con el comparador LM393
