# Fritzing sketch Ejercicio10-2 push buttons & 2 potentiometer & 1 LED (saved by Fritzing 0.9.3b)
breadboards: 1

parts:
  Parte1 = Arduino Uno (Rev3)
  ON/OFF = Pushbutton [package="[THT]"]
  Dirección_PULL-UP = Pushbutton [package="[THT]"]
  Velocidad_mot_delanteros = Rotary Potentiometer (Small) [maximum_resistance=10kΩ package=THT]
  Vel_mot_traseros = Rotary Potentiometer (Small) [maximum_resistance=10kΩ package=THT]
  1_2x8_V_battery_pack = 2.1mm DC Barrel Jack  # not connected
  R5 = Resistor [tolerance=±5% resistance=10k package="0805 [SMD]"]
  LED1 = LED - 5mm [color="Red (633nm)" package="5 mm [THT]"]  # not connected
  R6 = Resistor [tolerance=±5% resistance=220 package=THT]

nets:
  N1: Parte1.A0, Vel_mot_traseros.wiper
  N2: Parte1.A1, Velocidad_mot_delanteros.wiper
  N3: Parte1.D10_PWM/SS, Dirección_PULL-UP.Pin_3, Dirección_PULL-UP.Pin_4
  N4: Parte1.D11_PWM/MOSI, R6.Pin_0
  N5: Parte1.D12/MISO, ON/OFF.Pin_1, ON/OFF.Pin_2, R5.Pin_0
  N6: Parte1.5V, ON/OFF.Pin_3, ON/OFF.Pin_4
  N7: Dirección_PULL-UP.Pin_1, Dirección_PULL-UP.Pin_2, R6.Pin_1

custom parts:
  2.1mm DC Barrel Jack: 2.1mm DC Barrel Jack with Thru-Hole Connectors (breadboardable)
