# Fritzing sketch Ejercicio13-MotorDC_cuentapulsos (saved by Fritzing 0.9.3b)
breadboards: 1

parts:
  Parte1 = Arduino Uno (Rev3)
  IC1 = L293D [package=THT]
  FR_motor = DC Motor
  ON/OFF = Pushbutton [package="[THT]"]
  Dirección = Pushbutton [package="[THT]"]
  R3 = Rotary Potentiometer (Small) [maximum_resistance=100kΩ package=THT]
  Parte2 = Arduino Uno (Rev3)
  FR_encoder = TCRT5000 (LM393) [chip_label=TCRT5000 package="DIP (Dual Inline) [THT]"]
  RR_encoder = TCRT5000 (LM393) [chip_label=TCRT5000 package="DIP (Dual Inline) [THT]"]
  RR_motor = DC Motor
  FL_encoder = TCRT5000 (LM393) [chip_label=TCRT5000 package="DIP (Dual Inline) [THT]"]
  FL_motor = DC Motor
  RL_motor = DC Motor
  IC2 = L293D [package=THT]
  R4 = Rotary Potentiometer (Small) [maximum_resistance=100kΩ package=THT]
  RL_encoder = TCRT5000 (LM393) [chip_label=TCRT5000 package="DIP (Dual Inline) [THT]"]
  JACK1 = 2.1mm Barrel Jack with Terminal Block  # not connected
  1_2x8_V_battery_pack = 2.1mm DC Barrel Jack  # not connected
  R5 = Resistor [tolerance=±5% resistance=10k package="0805 [SMD]"]

nets:
  N1: Parte1.D2, FR_encoder.D0
  N2: Parte1.D3_PWM, FL_encoder.D0, FL_encoder.A0
  VCC: Parte1.5V, IC1.+Vmotor, IC1.+V, R3.leg1, FR_encoder.Vcc, FL_encoder.Vcc, IC2.+Vmotor, IC2.+V, R5.Pin_1
  GND: Parte1.GND, IC1.0V, R3.leg2, FR_encoder.GND, FL_encoder.GND, IC2.0V, R4.leg2
  N3: IC1.Out_1_(_Controlled_by_Enable_1_), FL_motor.pin_2
  N4: IC1.Out_2_(_Controlled_by_Enable_1_), FL_motor.pin_1
  N5: IC1.Out_3_(_Controlled_by_Enable_2_), FR_motor.pin_2
  N6: IC1.Out_4_(_Controlled_by_Enable_2_), FR_motor.pin_1
  N7: ON/OFF.Pin_1, ON/OFF.Pin_2, R5.Pin_0
  N8: ON/OFF.Pin_3, ON/OFF.Pin_4
  N9: Dirección.Pin_1, Dirección.Pin_2
  N10: Dirección.Pin_3, Dirección.Pin_4
  N11: Parte2.D2, RR_encoder.D0
  N12: Parte2.D3_PWM, RL_encoder.D0
  3V3: Parte2.3V3, RL_encoder.Vcc
  5V: Parte2.5V, RR_encoder.Vcc
  GND_2: Parte2.GND, RR_encoder.GND, RL_encoder.GND
  N13: RR_motor.pin_1, IC2.Out_4_(_Controlled_by_Enable_2_)
  N14: RR_motor.pin_2, IC2.Out_3_(_Controlled_by_Enable_2_)
  N15: RL_motor.pin_1, IC2.Out_2_(_Controlled_by_Enable_1_)
  N16: RL_motor.pin_2, IC2.Out_1_(_Controlled_by_Enable_1_)

notes:
  Frontal [Front]
  Trasera [Rear]
  Izquierda [Left]
  Derecha [Right]

custom parts:
  TCRT5000 (LM393): Sensor de infrarrojos para seguir líneas. Válido también para representar encoder de pulsos: optoacoplador FC-03 (ó FZ0888) con el comparador LM393
  2.1mm DC Barrel Jack: 2.1mm DC Barrel Jack with Thru-Hole Connectors (breadboardable)
