# Fritzing sketch Ejercicio13-MotorDC_cuentapulsos (saved by Fritzing 0.9.3b)
breadboards: 1

parts:
  Parte1 = Arduino Uno (Rev3)
  IC1 = L293D [package=THT]
  FR_motor = DC Motor
  ON/OFF = Pushbutton [package="[THT]"]
  Dirección_PULL-UP = Pushbutton [package="[THT]"]
  Velocidad_mot_delanteros = Rotary Potentiometer (Small) [maximum_resistance=10kΩ package=THT]
  Parte2 = Arduino Uno (Rev3)
  FR_encoder = TCRT5000 (LM393) [chip_label=TCRT5000 package="DIP (Dual Inline) [THT]"]
  RR_encoder = TCRT5000 (LM393) [chip_label=TCRT5000 package="DIP (Dual Inline) [THT]"]
  RR_motor = DC Motor
  FL_encoder = TCRT5000 (LM393) [chip_label=TCRT5000 package="DIP (Dual Inline) [THT]"]
  FL_motor = DC Motor
  RL_motor = DC Motor
  IC2 = L293D [package=THT]
  Vel_mot_traseros = Rotary Potentiometer (Small) [maximum_resistance=10kΩ package=THT]
  RL_encoder = TCRT5000 (LM393) [chip_label=TCRT5000 package="DIP (Dual Inline) [THT]"]
  JACK1 = 2.1mm Barrel Jack with Terminal Block  # not connected
  1_2x8_V_battery_pack = 2.1mm DC Barrel Jack  # not connected
  R5 = Resistor [tolerance=±5% resistance=10k package="0805 [SMD]"]
  LED1 = LED - 5mm [color="Red (633nm)" package="5 mm [THT]"]  # not connected
  R6 = Resistor [tolerance=±5% resistance=220 package=THT]

nets:
  N1: Parte1.A0, Vel_mot_traseros.wiper
  N2: Parte1.A1, Velocidad_mot_delanteros.wiper
  N3: Parte1.D8, IC1.In_2, IC1.In_3
  N4: Parte1.D9_PWM, IC1.Enable_1, IC1.Enable_2
  N5: Parte1.D10_PWM/SS, Dirección_PULL-UP.Pin_3, Dirección_PULL-UP.Pin_4
  N6: Parte1.D11_PWM/MOSI, R6.Pin_0
  N7: Parte1.D12/MISO, ON/OFF.Pin_1, ON/OFF.Pin_2, R5.Pin_0
  N8: Parte1.D2, FR_encoder.D0
  N9: Parte1.D3_PWM, FL_encoder.D0, FL_encoder.A0
  N10: Parte1.D4, IC2.In_1, IC2.In_4
  N11: Parte1.D5_PWM, IC2.In_2, IC2.In_3
  N12: Parte1.D6_PWM, IC2.Enable_1, IC2.Enable_2
  N13: Parte1.D7, IC1.In_1, IC1.In_4
  VCC: Parte1.5V, IC1.+Vmotor, IC1.+V, ON/OFF.Pin_3, ON/OFF.Pin_4, Velocidad_mot_delanteros.leg1, FR_encoder.Vcc, FL_encoder.Vcc, IC2.+Vmotor, IC2.+V
  GND: Parte1.GND, IC1.0V, Velocidad_mot_delanteros.leg2, FR_encoder.GND, FL_encoder.GND, IC2.0V, Vel_mot_traseros.leg2
  N14: IC1.Out_1_(_Controlled_by_Enable_1_), FL_motor.pin_2
  N15: IC1.Out_2_(_Controlled_by_Enable_1_), FL_motor.pin_1
  N16: IC1.Out_3_(_Controlled_by_Enable_2_), FR_motor.pin_2
  N17: IC1.Out_4_(_Controlled_by_Enable_2_), FR_motor.pin_1
  N18: Dirección_PULL-UP.Pin_1, Dirección_PULL-UP.Pin_2, R6.Pin_1
  N19: Parte2.D2, RR_encoder.D0
  N20: Parte2.D3_PWM, RL_encoder.D0
  3V3: Parte2.3V3, RL_encoder.Vcc
  5V: Parte2.5V, RR_encoder.Vcc
  GND_2: Parte2.GND, RR_encoder.GND, RL_encoder.GND
  N21: RR_motor.pin_1, IC2.Out_4_(_Controlled_by_Enable_2_)
  N22: RR_motor.pin_2, IC2.Out_3_(_Controlled_by_Enable_2_)
  N23: RL_motor.pin_1, IC2.Out_2_(_Controlled_by_Enable_1_)
  N24: RL_motor.pin_2, IC2.Out_1_(_Controlled_by_Enable_1_)

notes:
  Frontal [Front]
  Trasera [Rear]
  Izquierda [Left]
  Derecha [Right]

custom parts:
  TCRT5000 (LM393): Sensor de infrarrojos para seguir líneas. Válido también para representar encoder de pulsos: optoacoplador FC-03 (ó FZ0888) con el comparador LM393
  2.1mm DC Barrel Jack: 2.1mm DC Barrel Jack with Thru-Hole Connectors (breadboardable)
