# Fritzing sketch Ejercicio14-Interfaz_Processing (saved by Fritzing 0.9.3b)
breadboards: 1

parts:
  Parte1 = Arduino Uno (Rev3)
  DHT1 = DHT11 Humitidy and Temperature Sensor
  R1 = Resistor [tolerance=±5% resistance=220 package=THT]
  LED1 = LED - 5mm [color="Green (555nm)" package="5 mm [THT]"]  # not connected

nets:
  N1: Parte1.D2, DHT1.DATA
  5V: Parte1.5V, DHT1.VDD
  GND: Parte1.GND, DHT1.GND, R1.Pin_1

custom parts:
  DHT11 Humitidy and Temperature Sensor: DHT11 Humidity and Temperature Sensor
